# Fritzing sketch StandAlone328 (saved by Fritzing 0.9.3b)
circuit board: 8.46667cm x 5.64444cm
breadboards: 1

parts:
  U1 = atmega328 [package=dip]
  R1 = Resistor [tolerance=±5% resistance=10k package=THT]
  C1 = Capacitor [package=cap-pth-small2]
  C2 = Capacitor [package=cap-pth-small2]
  U2 = Voltage Regulator - 3.3V [package="TO220 [THT]"]
  C3 = Capacitor Polarized [package=cpol-radial-10uf-25v]
  C4 = Capacitor Polarized [package=cpol-radial-10uf-25v]
  VCC1 = 4 x AAA Battery Mount  # not connected
  JP1 = Header 4 [package=molex-1x4_lock]
  XTAL1 = Crystal [frequency="8 MHz" package=THT]
  J1 = AVR ISP 6 Pin [package=2x3-ns]
  JP2 = Header 2 [package=springterminal-2.54mm-2]

nets:
  N1: U1.RESET, R1.Pin_0, J1.5
  N2: U1.VCC, U1.AVCC, U1.AREF, R1.Pin_1, U2.output_voltage, C4.+, JP1.1, J1.2
  GND: U1.GND, C1.2, C2.2, U2.GND, C3.-, C4.-, JP1.2, J1.6, JP2.2
  N3: U1.XLAT1, C1.1, XTAL1.pin_0
  N4: U1.XLAT2, C2.1, XTAL1.pin_1
  N5: U1.D11_(PWM), J1.4
  N6: U1.D12, J1.1
  N7: U1.D13, J1.3
  N8: U1.A4, JP1.4
  N9: U1.A5, JP1.3
  N10: U2.input_voltage, C3.+, JP2.1
